# Fritzing sketch I&D (saved by Fritzing 0.9.3b)
breadboards: 1

parts:
  R1 = Resistor [tolerance=±5% resistance=10k package=THT]
  부품1 = Arduino Nano (Rev3.0)
  R3 = Resistor [tolerance=±5% resistance=10k package=THT]
  R4 = Resistor [tolerance=±5% resistance=10k package=THT]
  S2 = Pushbutton [package="[THT]"]
  S1 = Pushbutton [package="[THT]"]
  S3 = Pushbutton [package="[THT]"]
  R5 = Resistor [tolerance=±5% resistance=10k package=THT]
  S4 = Pushbutton [package="[THT]"]
  IC1 = IC, DIP package, 12 pins [chip_label="For motor"]
  M1 = Stepper Motor - Unipolar
  IC2 = IC, DIP package, 12 pins [chip_label="For motor"]
  M3 = Stepper Motor - Unipolar
  Power_plug1 = Power plug

nets:
  N1: R1.Pin_0, 부품1.5V, R3.Pin_0, R4.Pin_0, R5.Pin_0
  N2: R1.Pin_1, 부품1.D6, S1.Pin_3, S1.Pin_4
  GND: 부품1.GND, S2.Pin_1, S2.Pin_2, S1.Pin_1, S1.Pin_2, S3.Pin_1, S3.Pin_2, S4.Pin_1, S4.Pin_2, IC1.pin8, IC1.pin10, IC2.pin8, IC2.pin10, Power_plug1.GND
  N3: 부품1.D3, R5.Pin_1, S4.Pin_3, S4.Pin_4
  N4: 부품1.D4, R4.Pin_1, S3.Pin_3, S3.Pin_4
  N5: 부품1.D5, R3.Pin_1, S2.Pin_3, S2.Pin_4
  N6: 부품1.D7, IC2.pin12
  N7: 부품1.D8, IC2.pin11
  N8: 부품1.D9, IC2.pin9
  N9: 부품1.D10, IC1.pin12
  N10: 부품1.D11/MOSI, IC1.pin11
  N11: 부품1.D12/MISO, IC1.pin9
  N12: IC1.pin1, M1.D
  N13: IC1.pin2, M1.COMMON_2
  N14: IC1.pin3, M1.B
  N15: IC1.pin4, M1.A
  N16: IC1.pin5, M1.COMMON_1
  N17: IC1.pin6, M1.C
  N18: IC1.pin7, IC2.pin7, Power_plug1.VCC
  N19: IC2.pin1, M3.D
  N20: IC2.pin2, M3.COMMON_2
  N21: IC2.pin3, M3.B
  N22: IC2.pin4, M3.A
  N23: IC2.pin5, M3.COMMON_1
  N24: IC2.pin6, M3.C
